// Logisim project datapath.circ as structural Verilog: 1 circuit, main circuit main
module main (
);

  wire main_control_input_splitter_1_p2, main_control_input_splitter_1_p5, registerfile_1_p5;
  wire [2:0] main_control_input_splitter_1_p3, main_control_input_splitter_1_p6, multiplexer_1_out;
  wire [4:0] main_control_input_splitter_1_p4;
  wire [15:0] rom_1_data;
  wire [31:0] alu_1_p4, bit_extender_1_out, DataMemory_dout, multiplexer_2_out, registerfile_1_p1,
       registerfile_1_p6;

  ROM #(.addrWidth(20), .dataWidth(16)) rom_1 (.data(rom_1_data));  // open: addr
  // Main_Control_Input_Splitter main_control_input_splitter_1: pin names not known; wires that end beside it: rom_1_data, main_control_input_splitter_1_p2, main_control_input_splitter_1_p3, main_control_input_splitter_1_p4, main_control_input_splitter_1_p5, main_control_input_splitter_1_p6
  Multiplexer #(.width(3)) multiplexer_1 (
    .in0(main_control_input_splitter_1_p3), .in1(main_control_input_splitter_1_p6), .out(multiplexer_1_out));  // open: sel
  assign bit_extender_1_out = {{27{main_control_input_splitter_1_p4[4]}}, main_control_input_splitter_1_p4};  // Bit_Extender bit_extender_1
  // registerFile registerfile_1: pin names not known; wires that end beside it: registerfile_1_p1, main_control_input_splitter_1_p2, main_control_input_splitter_1_p3, multiplexer_1_out, registerfile_1_p5, registerfile_1_p6
  Multiplexer #(.width(32)) multiplexer_2 (
    .in0(registerfile_1_p6), .in1(bit_extender_1_out), .out(multiplexer_2_out));  // open: sel
  // ALU alu_1: pin names not known; wires that end beside it: registerfile_1_p5, multiplexer_2_out, main_control_input_splitter_1_p5, alu_1_p4
  RAM #(.addrWidth(18), .dataWidth(32)) DataMemory (
    .addr(alu_1_p4[19:2]), .din(registerfile_1_p6), .dout(DataMemory_dout));  // open: we, oe, clk
  Multiplexer #(.width(32)) multiplexer_3 (
    .in0(alu_1_p4), .in1(DataMemory_dout), .out(registerfile_1_p1));  // open: sel
endmodule
