// Logisim project pc.circ as structural Verilog: 1 circuit, main circuit Program_Counter
module Program_Counter (
  input  [19:0] PC_Input,
  output [19:0] PC,
  output [19:0] PC_Plus_2
);

  wire clock_1_out;

  Register #(.width(20)) register_1 (.D(PC_Input), .Q(PC), .clr(clock_1_out));  // open: en, clk
  Clock clock_1 (.out(clock_1_out));
  Adder #(.width(20)) adder_1 (.a(PC), .b(20'h2), .out(PC_Plus_2));  // open: cin, cout
endmodule
